# Fritzing sketch Projet_schema_pince (saved by Fritzing 0.9.3b)
breadboards: 1

parts:
  Composant1 = Arduino Uno (Rev3)
  IC1 = LM324 [package=dil16]
  C1 = Ceramic Capacitor [capacitance=100nF package="100 mil [THT, multilayer]"]
  R1 = Resistor [tolerance=±5% resistance=220 package=THT]
  C2 = Tantalum Capacitor [capacitance=1μF package="100 mil [THT, tantalum]"]
  R2 = Resistor [tolerance=±5% resistance=220 package=THT]
  C3 = Ceramic Capacitor [capacitance=100nF package="100 mil [THT, multilayer]"]
  R3 = Resistor [tolerance=±5% resistance=220 package=THT]
  R5 = Resistor [tolerance=±5% resistance=220 package=THT]
  R6 = Resistor [tolerance=±5% resistance=220 package=THT]
  R7 = Resistor [tolerance=±5% resistance=220 package=THT]
  C4 = Tantalum Capacitor [capacitance=1μF package="100 mil [THT, tantalum]"]
  P1 = S1133 Si Photodiode [package="8mm Ceramic [THT]"]
  Q2 = NPN-Transistor [package="SOT-23 [SMD]"]

nets (from the schematic view):
  N1: Composant1.5V, R7.Pin_0, Q2.1
  N2: Composant1.GND, R1.Pin_1, R5.Pin_0, R7.Pin_1, C4.+, P1.anode
  N3: IC1.OUT1, C1.1, C2.+
  N4: IC1.IN1-, C1.0, R1.Pin_0
  N5: IC1.IN1+, R5.Pin_1, C4.-
  N6: IC1.GND, R2.Pin_1
  N7: IC1.IN4+, C2.-, R2.Pin_0
  N8: IC1.IN4-, C3.0, R3.Pin_0
  N9: IC1.OUT4, R3.Pin_1
  N10: C3.1, R6.Pin_1

custom parts:
  LM324: LM324 Quad OpAmp
